# Fritzing sketch gesture switch (saved by Fritzing 0.9.3b)
breadboards: 1

parts:
  Raspberry_Pi_1 = Raspberry Pi 3 [part_number=RPI-3-V1.2]
  TOF_sensor = Adafruit VL530X Time of Flight Distance Sensor [part_number="Adafruit #3317"]
  J1 = Piezo Speaker
  R1 = Resistor [tolerance=±5% resistance=220 package="1206 [SMD]"]
  R5 = Resistor [tolerance=±5% resistance=220 package="1206 [SMD]"]
  LED3 = RGB LED (com. cathode, rbg) [package="5 mm [THT]"]
  R6 = Resistor [tolerance=±5% resistance=220 package="1206 [SMD]"]

nets:
  3V3: Raspberry_Pi_1.3v3, TOF_sensor.VCC
  N1: Raspberry_Pi_1.GPIO2, TOF_sensor.SDA
  N2: Raspberry_Pi_1.GPIO3, TOF_sensor.SCL
  GND: Raspberry_Pi_1.GND, TOF_sensor.GND, J1.pin1, LED3.common_cathode
  N3: Raspberry_Pi_1.GIPO21, J1.pin2
  N4: Raspberry_Pi_1.GIPO18, R5.Pin_1
  N5: Raspberry_Pi_1.GIPO15, R6.Pin_1
  N6: Raspberry_Pi_1.GIPO14, R1.Pin_1
  N7: R1.Pin_0, LED3.red_anode
  N8: R5.Pin_0, LED3.green_anode
  N9: LED3.blue_anode, R6.Pin_0

custom parts:
  Adafruit VL530X Time of Flight Distance Sensor: The VL53L0X is a Time of Flight distance sensor like no other you've used! The sensor contains a very tiny invisible laser source, and a matching sensor. The VL53L0X can detect the "time of flight", or how long the light has taken to bounce back to the sensor. Since it uses a very narrow light source, it is good for determining distance of only the surface directly in front of it. Unlike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
